# Fritzing sketch Progetto03 (saved by Fritzing 0.9.3b)
breadboards: 1

parts:
  U1 = ESP8266 WiFi Module [part_number=ESP8266]
  R1 = Rotary Potentiometer (Small) [maximum_resistance=100kΩ package=THT]

nets:
  N1: U1.VCC, R1.leg2
  N2: U1.GND, R1.leg1
  N3: U1.ADC_0, R1.wiper
